# Fritzing sketch NanoGPIO (saved by Fritzing 0.9.3b)
breadboards: 1

parts:
  J1 = molex pin header, 20 pins [form=molex]
  J2 = molex pin header, 20 pins [form=molex]
  R1 = Resistor [tolerance=±5% resistance=220 package=THT]
  S1 = Pushbutton [package="[THT]"]
  R2 = Resistor [tolerance=±5% resistance=10k package=THT]
  LED1 = LED - 5mm [color="Red (633nm)" package="5 mm [THT]"]

nets:
  N1: J1.pin1, R2.Pin_0
  N2: J1.pin5, S1.Pin_1, S1.Pin_2, LED1.cathode
  N3: J1.pin17, R1.Pin_1
  N4: J2.pin19, S1.Pin_3, S1.Pin_4, R2.Pin_1
  N5: R1.Pin_0, LED1.anode

notes:
  NVIDIA Jetson Nano GPIO
