# Fritzing sketch Ultrasonic (saved by Fritzing 0.9.3b)
breadboards: 1

parts:
  J1 = molex pin header, 20 pins [form=molex]
  J2 = molex pin header, 20 pins [form=molex]
  HC-SR04_Sensor_1 = HC-SR04 Ultrasonic Distance Sensor

nets:
  N1: J1.pin5, HC-SR04_Sensor_1.GND
  N2: J1.pin17, HC-SR04_Sensor_1.TRIG
  N3: J2.pin1, HC-SR04_Sensor_1.VCC
  N4: J2.pin19, HC-SR04_Sensor_1.ECHO

notes:
  NVIDIA Jetson Nano GPIO
