# Fritzing sketch cds (saved by Fritzing 0.9.3b)
breadboards: 1

parts:
  J1 = molex pin header, 20 pins [form=molex]
  J2 = molex pin header, 20 pins [form=molex]
  R1 = Resistor [tolerance=±5% resistance=220 package=THT]
  R2 = Resistor [tolerance=±5% resistance=10k package=THT]
  LED1 = LED - 5mm [color="Red (633nm)" package="5 mm [THT]"]
  R3 = PHOTOCELL [package=photocell-kit]

nets:
  N1: J1.pin1, R2.Pin_1
  N2: J1.pin5, J2.pin19, LED1.cathode, R3.P$2
  N3: J1.pin17, R1.Pin_1
  N4: R1.Pin_0, LED1.anode
  N5: R2.Pin_0, R3.P$1

notes:
  NVIDIA Jetson Nano GPIO
