# Fritzing sketch led (saved by Fritzing 0.9.3b)
breadboards: 1

parts:
  J1 = molex pin header, 20 pins [form=molex]
  J2 = molex pin header, 20 pins [form=molex]  # not connected
  R1 = Resistor [tolerance=±5% resistance=220 package=THT]
  LED1 = LED - 5mm [color="Red (633nm)" package="5 mm [THT]"]

nets:
  N1: J1.pin5, LED1.cathode
  N2: J1.pin17, R1.Pin_1
  N3: R1.Pin_0, LED1.anode

notes:
  NVIDIA Jetson Nano GPIO
